# Fritzing sketch demo (saved by Fritzing 0.9.10b)
breadboards: 1

parts:
  PWM1 = PCA9685 16x12-bit PWM Breakout
  Part1 = Arduino Nano (Rev3.0)
  LED3 = LED - 3mm [color="Red (633nm)" current=0.030 package="3 mm [THT]"]
  LED4 = LED - 3mm [color="Green (565nm)" current=0.030 package="3 mm [THT]"]
  LED1 = LED - 3mm [color="Blue (430nm)" current=0.030 package="3 mm [THT]"]
  LED2 = LED - 3mm [color="Yellow (592nm)" current=0.030 package="3 mm [THT]"]

nets:
  N1: PWM1.no_name_yet#12, LED3.anode
  N2: PWM1.no_name_yet#13, LED4.anode
  N3: PWM1.no_name_yet#14, LED1.anode
  N4: PWM1.no_name_yet#15, LED2.anode
  N5: PWM1.no_name_yet#601, Part1.GND, LED3.cathode, LED4.cathode, LED1.cathode, LED2.cathode
  N6: PWM1.no_name_yet#603, Part1.A5
  N7: PWM1.no_name_yet#604, Part1.A4
  N8: PWM1.no_name_yet#605, Part1.5V
